// Logisim project ULA 32bits.circ as structural Verilog: 12 circuits, main circuit main
module \Célula  (
  input  ESQUERDA,
  input  DIREITA,
  input  A,
  input  B,
  input  [4:0] in_5,
  input  VEM_1,
  output S,
  output VAI_1
);

  wire adder_1_cout, adder_1_out, and_1_out, and_2_out, nand_1_out, or_1_out, subtractor_1_bout,
       subtractor_1_out, xor_1_out;

  and and_1 (and_1_out, A, B);
  or or_1 (or_1_out, A, B);
  nand nand_1 (nand_1_out, A, B);
  xor xor_1 (xor_1_out, A, B);
  Adder #(.width(1)) adder_1 (.a(A), .b(B), .out(adder_1_out), .cin(VEM_1), .cout(adder_1_cout));
  Subtractor #(.width(1)) subtractor_1 (.a(A), .b(B), .out(subtractor_1_out), .bin(VEM_1), .bout(subtractor_1_bout));
  and and_2 (and_2_out, ~in_5[4], ~in_5[3], in_5[2], in_5[1], ~in_5[0]);  // AND_Gate
  Multiplexer #(.enable("false")) multiplexer_1 (
    .in0(adder_1_cout), .in1(subtractor_1_bout), .out(VAI_1), .sel(and_2_out));
  Multiplexer #(.select(5), .enable("false")) multiplexer_2 (
    .in0(and_1_out), .in1(or_1_out), .in2(nand_1_out), .in3(xor_1_out), .in4(adder_1_out), .in5(adder_1_out),
    .in6(subtractor_1_out), .in7(DIREITA), .in8(DIREITA), .in9(ESQUERDA), .out(S), .sel(in_5));  // open: in10, in11, in12, in13, in14, in15, in16, in17, in18, in19, in20, in21, in22, in23, in24, in25, in26, in27, in28, in29, in30, in31
endmodule

module ULA (
  input  [31:0] A,
  input  [4:0] SELETOR,
  input  [31:0] B,
  output OVERFLOW,
  output [31:0] S,
  output ZERO
);

  wire and_1_out, \célula_1_vai_1 , \célula_2_vai_1 , \célula_3_vai_1 , \célula_4_vai_1 , \célula_5_vai_1 ,
       \célula_6_vai_1 , \célula_7_vai_1 , \célula_8_vai_1 , \célula_9_vai_1 , \célula_10_vai_1 ,
       \célula_11_vai_1 , \célula_12_vai_1 , \célula_13_vai_1 , \célula_14_vai_1 , \célula_15_vai_1 ,
       \célula_16_vai_1 , \célula_17_vai_1 , \célula_18_vai_1 , \célula_19_vai_1 , \célula_20_vai_1 ,
       \célula_21_vai_1 , \célula_22_vai_1 , \célula_23_vai_1 , \célula_24_vai_1 , \célula_25_vai_1 ,
       \célula_26_vai_1 , \célula_27_vai_1 , \célula_28_vai_1 , \célula_29_vai_1 , \célula_30_vai_1 ,
       \célula_31_vai_1 , \célula_mais_significativa_1_vai_1 , overflow_1_out_4;

  \Célula_mais_significativa  \célula_mais_significativa_1  (
    .ESQUERDA(A[30]), .A(A[31]), .B(B[31]), .VEM_1(\célula_1_vai_1 ), .in_5(SELETOR),
    .\DIREITA_ARITMÉTICA (A[31]), .DIREITA(1'b0), .S(S[31]), .VAI_1(\célula_mais_significativa_1_vai_1 ));
  Multiplexer #(.enable("false")) multiplexer_1 (
    .in0(overflow_1_out_4), .in1(\célula_mais_significativa_1_vai_1 ), .out(OVERFLOW), .sel(and_1_out));
  and and_1 (and_1_out, ~SELETOR[0], ~SELETOR[1], SELETOR[2], ~SELETOR[3], ~SELETOR[4]);  // AND_Gate
  Overflow overflow_1 (.A(A[31]), .B(B[31]), .S(S[31]), .out_4(overflow_1_out_4));
  \Célula  \célula_1  (
    .ESQUERDA(A[29]), .A(A[30]), .B(B[30]), .VEM_1(\célula_2_vai_1 ), .in_5(SELETOR), .DIREITA(A[31]),
    .S(S[30]), .VAI_1(\célula_1_vai_1 ));
  \Célula  \célula_2  (
    .ESQUERDA(A[28]), .A(A[29]), .B(B[29]), .VEM_1(\célula_3_vai_1 ), .in_5(SELETOR), .DIREITA(A[30]),
    .S(S[29]), .VAI_1(\célula_2_vai_1 ));
  \Célula  \célula_3  (
    .ESQUERDA(A[27]), .A(A[28]), .B(B[28]), .VEM_1(\célula_4_vai_1 ), .in_5(SELETOR), .DIREITA(A[29]),
    .S(S[28]), .VAI_1(\célula_3_vai_1 ));
  \Célula  \célula_4  (
    .ESQUERDA(A[26]), .A(A[27]), .B(B[27]), .VEM_1(\célula_5_vai_1 ), .in_5(SELETOR), .DIREITA(A[28]),
    .S(S[27]), .VAI_1(\célula_4_vai_1 ));
  \Célula  \célula_5  (
    .ESQUERDA(A[25]), .A(A[26]), .B(B[26]), .VEM_1(\célula_6_vai_1 ), .in_5(SELETOR), .DIREITA(A[27]),
    .S(S[26]), .VAI_1(\célula_5_vai_1 ));
  \Célula  \célula_6  (
    .ESQUERDA(A[24]), .A(A[25]), .B(B[25]), .VEM_1(\célula_7_vai_1 ), .in_5(SELETOR), .DIREITA(A[26]),
    .S(S[25]), .VAI_1(\célula_6_vai_1 ));
  \Célula  \célula_7  (
    .ESQUERDA(A[23]), .A(A[24]), .B(B[24]), .VEM_1(\célula_8_vai_1 ), .in_5(SELETOR), .DIREITA(A[25]),
    .S(S[24]), .VAI_1(\célula_7_vai_1 ));
  \Célula  \célula_8  (
    .ESQUERDA(A[22]), .A(A[23]), .B(B[23]), .VEM_1(\célula_9_vai_1 ), .in_5(SELETOR), .DIREITA(A[24]),
    .S(S[23]), .VAI_1(\célula_8_vai_1 ));
  \Célula  \célula_9  (
    .ESQUERDA(A[21]), .A(A[22]), .B(B[22]), .VEM_1(\célula_10_vai_1 ), .in_5(SELETOR), .DIREITA(A[23]),
    .S(S[22]), .VAI_1(\célula_9_vai_1 ));
  \Célula  \célula_10  (
    .ESQUERDA(A[20]), .A(A[21]), .B(B[21]), .VEM_1(\célula_11_vai_1 ), .in_5(SELETOR), .DIREITA(A[22]),
    .S(S[21]), .VAI_1(\célula_10_vai_1 ));
  \Célula  \célula_11  (
    .ESQUERDA(A[19]), .A(A[20]), .B(B[20]), .VEM_1(\célula_12_vai_1 ), .in_5(SELETOR), .DIREITA(A[21]),
    .S(S[20]), .VAI_1(\célula_11_vai_1 ));
  \Célula  \célula_12  (
    .ESQUERDA(A[18]), .A(A[19]), .B(B[19]), .VEM_1(\célula_13_vai_1 ), .in_5(SELETOR), .DIREITA(A[20]),
    .S(S[19]), .VAI_1(\célula_12_vai_1 ));
  \Célula  \célula_13  (
    .ESQUERDA(A[17]), .A(A[18]), .B(B[18]), .VEM_1(\célula_14_vai_1 ), .in_5(SELETOR), .DIREITA(A[19]),
    .S(S[18]), .VAI_1(\célula_13_vai_1 ));
  \Célula  \célula_14  (
    .ESQUERDA(A[16]), .A(A[17]), .B(B[17]), .VEM_1(\célula_15_vai_1 ), .in_5(SELETOR), .DIREITA(A[18]),
    .S(S[17]), .VAI_1(\célula_14_vai_1 ));
  \Célula  \célula_15  (
    .ESQUERDA(A[15]), .A(A[16]), .B(B[16]), .VEM_1(\célula_16_vai_1 ), .in_5(SELETOR), .DIREITA(A[17]),
    .S(S[16]), .VAI_1(\célula_15_vai_1 ));
  \Célula  \célula_16  (
    .ESQUERDA(A[14]), .A(A[15]), .B(B[15]), .VEM_1(\célula_17_vai_1 ), .in_5(SELETOR), .DIREITA(A[16]),
    .S(S[15]), .VAI_1(\célula_16_vai_1 ));
  \Célula  \célula_17  (
    .ESQUERDA(A[13]), .A(A[14]), .B(B[14]), .VEM_1(\célula_18_vai_1 ), .in_5(SELETOR), .DIREITA(A[15]),
    .S(S[14]), .VAI_1(\célula_17_vai_1 ));
  \Célula  \célula_18  (
    .ESQUERDA(A[12]), .A(A[13]), .B(B[13]), .VEM_1(\célula_19_vai_1 ), .in_5(SELETOR), .DIREITA(A[14]),
    .S(S[13]), .VAI_1(\célula_18_vai_1 ));
  \Célula  \célula_19  (
    .ESQUERDA(A[11]), .A(A[12]), .B(B[12]), .VEM_1(\célula_20_vai_1 ), .in_5(SELETOR), .DIREITA(A[13]),
    .S(S[12]), .VAI_1(\célula_19_vai_1 ));
  \Célula  \célula_20  (
    .ESQUERDA(A[10]), .A(A[11]), .B(B[11]), .VEM_1(\célula_21_vai_1 ), .in_5(SELETOR), .DIREITA(A[12]),
    .S(S[11]), .VAI_1(\célula_20_vai_1 ));
  \Célula  \célula_21  (
    .ESQUERDA(A[9]), .A(A[10]), .B(B[10]), .VEM_1(\célula_22_vai_1 ), .in_5(SELETOR), .DIREITA(A[11]),
    .S(S[10]), .VAI_1(\célula_21_vai_1 ));
  \Célula  \célula_22  (
    .ESQUERDA(A[8]), .A(A[9]), .B(B[9]), .VEM_1(\célula_23_vai_1 ), .in_5(SELETOR), .DIREITA(A[10]),
    .S(S[9]), .VAI_1(\célula_22_vai_1 ));
  \Célula  \célula_23  (
    .ESQUERDA(A[7]), .A(A[8]), .B(B[8]), .VEM_1(\célula_24_vai_1 ), .in_5(SELETOR), .DIREITA(A[9]), .S(S[8]),
    .VAI_1(\célula_23_vai_1 ));
  \Célula  \célula_24  (
    .ESQUERDA(A[6]), .A(A[7]), .B(B[7]), .VEM_1(\célula_25_vai_1 ), .in_5(SELETOR), .DIREITA(A[8]), .S(S[7]),
    .VAI_1(\célula_24_vai_1 ));
  \Célula  \célula_25  (
    .ESQUERDA(A[5]), .A(A[6]), .B(B[6]), .VEM_1(\célula_26_vai_1 ), .in_5(SELETOR), .DIREITA(A[7]), .S(S[6]),
    .VAI_1(\célula_25_vai_1 ));
  \Célula  \célula_26  (
    .ESQUERDA(A[4]), .A(A[5]), .B(B[5]), .VEM_1(\célula_27_vai_1 ), .in_5(SELETOR), .DIREITA(A[6]), .S(S[5]),
    .VAI_1(\célula_26_vai_1 ));
  and and_2 (ZERO, ~S[31], ~S[30], ~S[29], ~S[28], ~S[27], ~S[26], ~S[25], ~S[24], ~S[23], ~S[22], ~S[21], ~S[20], ~S[19], ~S[18], ~S[17], ~S[16], ~S[15], ~S[14], ~S[13], ~S[12], ~S[11], ~S[10], ~S[9], ~S[8], ~S[7], ~S[6], ~S[5], ~S[4], ~S[3], ~S[2], ~S[1], ~S[0]);  // AND_Gate
  \Célula  \célula_27  (
    .ESQUERDA(A[3]), .A(A[4]), .B(B[4]), .VEM_1(\célula_28_vai_1 ), .in_5(SELETOR), .DIREITA(A[5]), .S(S[4]),
    .VAI_1(\célula_27_vai_1 ));
  \Célula  \célula_28  (
    .ESQUERDA(A[2]), .A(A[3]), .B(B[3]), .VEM_1(\célula_29_vai_1 ), .in_5(SELETOR), .DIREITA(A[4]), .S(S[3]),
    .VAI_1(\célula_28_vai_1 ));
  \Célula  \célula_29  (
    .ESQUERDA(A[1]), .A(A[2]), .B(B[2]), .VEM_1(\célula_30_vai_1 ), .in_5(SELETOR), .DIREITA(A[3]), .S(S[2]),
    .VAI_1(\célula_29_vai_1 ));
  \Célula  \célula_30  (
    .ESQUERDA(A[0]), .A(A[1]), .B(B[1]), .VEM_1(\célula_31_vai_1 ), .in_5(SELETOR), .DIREITA(A[2]), .S(S[1]),
    .VAI_1(\célula_30_vai_1 ));
  \Célula  \célula_31  (
    .ESQUERDA(1'b0), .A(A[0]), .B(B[0]), .VEM_1(1'b0), .in_5(SELETOR), .DIREITA(A[1]), .S(S[0]),
    .VAI_1(\célula_31_vai_1 ));
endmodule

module \Célula_mais_significativa  (
  input  ESQUERDA,
  input  DIREITA,
  input  A,
  input  B,
  input  [4:0] in_5,
  input  VEM_1,
  input  \DIREITA_ARITMÉTICA ,
  output S,
  output VAI_1
);

  wire adder_1_cout, adder_1_out, and_1_out, and_2_out, nand_1_out, or_1_out, subtractor_1_bout,
       subtractor_1_out, xor_1_out;

  and and_1 (and_1_out, A, B);
  or or_1 (or_1_out, A, B);
  nand nand_1 (nand_1_out, A, B);
  xor xor_1 (xor_1_out, A, B);
  Adder #(.width(1)) adder_1 (.a(A), .b(B), .out(adder_1_out), .cin(VEM_1), .cout(adder_1_cout));
  Subtractor #(.width(1)) subtractor_1 (.a(A), .b(B), .out(subtractor_1_out), .bin(VEM_1), .bout(subtractor_1_bout));
  and and_2 (and_2_out, ~in_5[4], ~in_5[3], in_5[2], in_5[1], ~in_5[0]);  // AND_Gate
  Multiplexer #(.enable("false")) multiplexer_1 (
    .in0(adder_1_cout), .in1(subtractor_1_bout), .out(VAI_1), .sel(and_2_out));
  Multiplexer #(.select(5), .enable("false")) multiplexer_2 (
    .in0(and_1_out), .in1(or_1_out), .in2(nand_1_out), .in3(xor_1_out), .in4(adder_1_out), .in5(adder_1_out),
    .in6(subtractor_1_out), .in7(DIREITA), .in8(\DIREITA_ARITMÉTICA ), .in9(ESQUERDA), .out(S), .sel(in_5));  // open: in10, in11, in12, in13, in14, in15, in16, in17, in18, in19, in20, in21, in22, in23, in24, in25, in26, in27, in28, in29, in30, in31
endmodule

module Overflow (
  input  A,
  input  B,
  input  S,
  output out_4
);

  wire and_1_out, and_2_out;

  and and_1 (and_1_out, ~A, S, ~B);  // AND_Gate
  and and_2 (and_2_out, A, ~S, B);  // AND_Gate
  or or_1 (out_4, and_1_out, and_2_out);
endmodule

module Shifter (
  input  A31,
  input  A30,
  input  A29,
  input  A28,
  input  A27,
  input  A26,
  input  A25,
  input  A24,
  input  A23,
  input  A22,
  input  A21,
  input  A20,
  input  A19,
  input  A18,
  input  A17,
  input  A16,
  input  A15,
  input  A14,
  input  A13,
  input  A12,
  input  A11,
  input  A10,
  input  A09,
  input  A08,
  input  A07,
  input  A06,
  input  A05,
  input  A04,
  input  A03,
  input  A02,
  input  A01,
  input  A00,
  input  ESQUERDA,
  input  DIREITA,
  output S31,
  output S30,
  output S29,
  output S28,
  output S27,
  output S26,
  output S25,
  output S24,
  output S23,
  output S22,
  output S21,
  output S20,
  output S19,
  output S18,
  output S17,
  output S16,
  output S15,
  output A14_2,
  output S13,
  output S12,
  output S11,
  output S10,
  output S09,
  output S08,
  output S07,
  output S06,
  output S05,
  output S04,
  output S03,
  output S02,
  output S01,
  output S00
);

  Multiplexer #(.select(2), .enable("false")) multiplexer_1 (
    .in0(A31), .in1(A30), .in2(1'b0), .out(S31), .sel({DIREITA, ESQUERDA}));  // open: in3
  Multiplexer #(.select(2), .enable("false")) multiplexer_2 (
    .in0(A30), .in1(A29), .in2(A29), .out(S30), .sel({DIREITA, ESQUERDA}));  // open: in3
  Multiplexer #(.select(2), .enable("false")) multiplexer_3 (
    .in0(A29), .in1(A28), .in2(A30), .out(S29), .sel({DIREITA, ESQUERDA}));  // open: in3
  Multiplexer #(.select(2), .enable("false")) multiplexer_4 (
    .in0(A28), .in1(A27), .in2(A29), .out(S28), .sel({DIREITA, ESQUERDA}));  // open: in3
  Multiplexer #(.select(2), .enable("false")) multiplexer_5 (
    .in0(A27), .in1(A26), .in2(A28), .out(S27), .sel({DIREITA, ESQUERDA}));  // open: in3
  Multiplexer #(.select(2), .enable("false")) multiplexer_6 (
    .in0(A26), .in1(A25), .in2(A27), .out(S26), .sel({DIREITA, ESQUERDA}));  // open: in3
  Multiplexer #(.select(2), .enable("false")) multiplexer_7 (
    .in0(A25), .in1(A24), .in2(A26), .out(S25), .sel({DIREITA, ESQUERDA}));  // open: in3
  Multiplexer #(.select(2), .enable("false")) multiplexer_8 (
    .in0(A24), .in1(A23), .in2(A25), .out(S24), .sel({DIREITA, ESQUERDA}));  // open: in3
  Multiplexer #(.select(2), .enable("false")) multiplexer_9 (
    .in0(A23), .in1(A22), .in2(A24), .out(S23), .sel({DIREITA, ESQUERDA}));  // open: in3
  Multiplexer #(.select(2), .enable("false")) multiplexer_10 (
    .in0(A22), .in1(A21), .in2(A23), .out(S22), .sel({DIREITA, ESQUERDA}));  // open: in3
  Multiplexer #(.select(2), .enable("false")) multiplexer_11 (
    .in0(A21), .in1(A20), .in2(A22), .out(S21), .sel({DIREITA, ESQUERDA}));  // open: in3
  Multiplexer #(.select(2), .enable("false")) multiplexer_12 (
    .in0(A20), .in1(A19), .in2(A21), .out(S20), .sel({DIREITA, ESQUERDA}));  // open: in3
  Multiplexer #(.select(2), .enable("false")) multiplexer_13 (
    .in0(A19), .in1(A18), .in2(A20), .out(S19), .sel({DIREITA, ESQUERDA}));  // open: in3
  Multiplexer #(.select(2), .enable("false")) multiplexer_14 (
    .in0(A18), .in1(A17), .in2(A19), .out(S18), .sel({DIREITA, ESQUERDA}));  // open: in3
  Multiplexer #(.select(2), .enable("false")) multiplexer_15 (
    .in0(A17), .in1(A16), .in2(A18), .out(S17), .sel({DIREITA, ESQUERDA}));  // open: in3
  Multiplexer #(.select(2), .enable("false")) multiplexer_16 (
    .in0(A16), .in1(A15), .in2(A17), .out(S16), .sel({DIREITA, ESQUERDA}));  // open: in3
  Multiplexer #(.select(2), .enable("false")) multiplexer_17 (
    .in0(A15), .in1(A14), .in2(A16), .out(S15), .sel({DIREITA, ESQUERDA}));  // open: in3
  Multiplexer #(.select(2), .enable("false")) multiplexer_18 (
    .in0(A14), .in1(A13), .in2(A15), .out(A14_2), .sel({DIREITA, ESQUERDA}));  // open: in3
  Multiplexer #(.select(2), .enable("false")) multiplexer_19 (
    .in0(A13), .in1(A12), .in2(A14), .out(S13), .sel({DIREITA, ESQUERDA}));  // open: in3
  Multiplexer #(.select(2), .enable("false")) multiplexer_20 (
    .in0(A12), .in1(A11), .in2(A13), .out(S12), .sel({DIREITA, ESQUERDA}));  // open: in3
  Multiplexer #(.select(2), .enable("false")) multiplexer_21 (
    .in0(A11), .in1(A10), .in2(A12), .out(S11), .sel({DIREITA, ESQUERDA}));  // open: in3
  Multiplexer #(.select(2), .enable("false")) multiplexer_22 (
    .in0(A10), .in1(A09), .in2(A11), .out(S10), .sel({DIREITA, ESQUERDA}));  // open: in3
  Multiplexer #(.select(2), .enable("false")) multiplexer_23 (
    .in0(A09), .in1(A08), .in2(A10), .out(S09), .sel({DIREITA, ESQUERDA}));  // open: in3
  Multiplexer #(.select(2), .enable("false")) multiplexer_24 (
    .in0(A08), .in1(A07), .in2(A09), .out(S08), .sel({DIREITA, ESQUERDA}));  // open: in3
  Multiplexer #(.select(2), .enable("false")) multiplexer_25 (
    .in0(A07), .in1(A06), .in2(A08), .out(S07), .sel({DIREITA, ESQUERDA}));  // open: in3
  Multiplexer #(.select(2), .enable("false")) multiplexer_26 (
    .in0(A06), .in1(A05), .in2(A07), .out(S06), .sel({DIREITA, ESQUERDA}));  // open: in3
  Multiplexer #(.select(2), .enable("false")) multiplexer_27 (
    .in0(A05), .in1(A04), .in2(A06), .out(S05), .sel({DIREITA, ESQUERDA}));  // open: in3
  Multiplexer #(.select(2), .enable("false")) multiplexer_28 (
    .in0(A04), .in1(A03), .in2(A05), .out(S04), .sel({DIREITA, ESQUERDA}));  // open: in3
  Multiplexer #(.select(2), .enable("false")) multiplexer_29 (
    .in0(A03), .in1(A02), .in2(A02), .out(S03), .sel({DIREITA, ESQUERDA}));  // open: in3
  Multiplexer #(.select(2), .enable("false")) multiplexer_30 (
    .in0(A02), .in1(A01), .in2(A03), .out(S02), .sel({DIREITA, ESQUERDA}));  // open: in3
  Multiplexer #(.select(2), .enable("false")) multiplexer_31 (
    .in0(A01), .in1(A00), .in2(A02), .out(S01), .sel({DIREITA, ESQUERDA}));  // open: in3
  Multiplexer #(.select(2), .enable("false")) multiplexer_32 (
    .in0(A00), .in1(1'b0), .in2(A01), .out(S00), .sel({DIREITA, ESQUERDA}));  // open: in3
endmodule

module Registrador (
  input  [31:0] dataOUT,
  input  WR,
  input  [31:0] S,
  input  [31:0] dataIN
);

  D_Flip_Flop d_ff_1 (.clk(dataIN[8]), .D(dataIN[0]), .Q(S[0]));  // open: Qn, preset, en, reset
  D_Flip_Flop d_ff_2 (.clk(dataIN[8]), .D(dataIN[8]), .Q(S[8]));  // open: Qn, preset, en, reset
  D_Flip_Flop d_ff_3 (.clk(dataIN[8]), .D(dataIN[16]), .Q(S[16]));  // open: Qn, preset, en, reset
  D_Flip_Flop d_ff_4 (.clk(dataIN[8]), .D(dataIN[24]), .Q(S[24]));  // open: Qn, preset, en, reset
  D_Flip_Flop d_ff_5 (.clk(dataIN[8]), .D(dataIN[1]), .Q(S[1]));  // open: Qn, preset, en, reset
  D_Flip_Flop d_ff_6 (.clk(dataIN[8]), .D(dataIN[9]), .Q(S[9]));  // open: Qn, preset, en, reset
  D_Flip_Flop d_ff_7 (.clk(dataIN[8]), .D(dataIN[17]), .Q(S[17]));  // open: Qn, preset, en, reset
  D_Flip_Flop d_ff_8 (.clk(dataIN[8]), .D(dataIN[25]), .Q(S[25]));  // open: Qn, preset, en, reset
  D_Flip_Flop d_ff_9 (.clk(dataIN[8]), .D(dataIN[2]), .Q(S[2]));  // open: Qn, preset, en, reset
  D_Flip_Flop d_ff_10 (.clk(dataIN[8]), .D(dataIN[10]), .Q(S[10]));  // open: Qn, preset, en, reset
  D_Flip_Flop d_ff_11 (.clk(dataIN[8]), .D(dataIN[18]), .Q(S[18]));  // open: Qn, preset, en, reset
  D_Flip_Flop d_ff_12 (.clk(dataIN[8]), .D(dataIN[26]), .Q(S[26]));  // open: Qn, preset, en, reset
  D_Flip_Flop d_ff_13 (.clk(dataIN[8]), .D(dataIN[3]), .Q(S[3]));  // open: Qn, preset, en, reset
  D_Flip_Flop d_ff_14 (.clk(dataIN[8]), .D(dataIN[11]), .Q(S[11]));  // open: Qn, preset, en, reset
  D_Flip_Flop d_ff_15 (.clk(dataIN[8]), .D(dataIN[19]), .Q(S[19]));  // open: Qn, preset, en, reset
  D_Flip_Flop d_ff_16 (.clk(dataIN[8]), .D(dataIN[27]), .Q(S[27]));  // open: Qn, preset, en, reset
  D_Flip_Flop d_ff_17 (.clk(dataIN[8]), .D(dataIN[4]), .Q(S[4]));  // open: Qn, preset, en, reset
  D_Flip_Flop d_ff_18 (.clk(dataIN[8]), .D(dataIN[12]), .Q(S[12]));  // open: Qn, preset, en, reset
  D_Flip_Flop d_ff_19 (.clk(dataIN[8]), .D(dataIN[20]), .Q(S[20]));  // open: Qn, preset, en, reset
  D_Flip_Flop d_ff_20 (.clk(dataIN[8]), .D(dataIN[28]), .Q(S[28]));  // open: Qn, preset, en, reset
  D_Flip_Flop d_ff_21 (.clk(dataIN[8]), .D(dataIN[5]), .Q(S[5]));  // open: Qn, preset, en, reset
  D_Flip_Flop d_ff_22 (.clk(dataIN[8]), .D(dataIN[13]), .Q(S[13]));  // open: Qn, preset, en, reset
  D_Flip_Flop d_ff_23 (.clk(dataIN[8]), .D(dataIN[21]), .Q(S[21]));  // open: Qn, preset, en, reset
  D_Flip_Flop d_ff_24 (.clk(dataIN[8]), .D(dataIN[29]), .Q(S[29]));  // open: Qn, preset, en, reset
  D_Flip_Flop d_ff_25 (.clk(dataIN[8]), .D(dataIN[6]), .Q(S[6]));  // open: Qn, preset, en, reset
  D_Flip_Flop d_ff_26 (.clk(dataIN[8]), .D(dataIN[14]), .Q(S[14]));  // open: Qn, preset, en, reset
  D_Flip_Flop d_ff_27 (.clk(dataIN[8]), .D(dataIN[22]), .Q(S[22]));  // open: Qn, preset, en, reset
  D_Flip_Flop d_ff_28 (.clk(dataIN[8]), .D(dataIN[30]), .Q(S[30]));  // open: Qn, preset, en, reset
  D_Flip_Flop d_ff_29 (.clk(dataIN[8]), .D(dataIN[7]), .Q(S[7]));  // open: Qn, preset, en, reset
  D_Flip_Flop d_ff_30 (.clk(dataIN[8]), .D(dataIN[15]), .Q(S[15]));  // open: Qn, preset, en, reset
  D_Flip_Flop d_ff_31 (.clk(dataIN[8]), .D(dataIN[23]), .Q(S[23]));  // open: Qn, preset, en, reset
  D_Flip_Flop d_ff_32 (.clk(dataIN[8]), .D(dataIN[31]), .Q(S[31]));  // open: Qn, preset, en, reset

  assign dataOUT = dataIN;
  assign WR = dataIN[8];
endmodule

module Banco_Registrador (
  input  [31:0] Data,
  input  [31:0] RSout,
  input  WR,
  input  [4:0] RS,
  input  [4:0] RegDEST,
  input  [31:0] RTout,
  input  [4:0] RT
);

  wire demultiplexer_1_out1, demultiplexer_1_out2, demultiplexer_1_out3, demultiplexer_1_out4,
       demultiplexer_1_out5, demultiplexer_1_out6, demultiplexer_1_out7, demultiplexer_1_out8,
       demultiplexer_1_out9, demultiplexer_1_out10, demultiplexer_1_out11, demultiplexer_1_out12,
       demultiplexer_1_out13, demultiplexer_1_out14, demultiplexer_1_out15, demultiplexer_1_out16,
       demultiplexer_1_out17, demultiplexer_1_out18, demultiplexer_1_out19, demultiplexer_1_out20,
       demultiplexer_1_out21, demultiplexer_1_out22, demultiplexer_1_out23, demultiplexer_1_out24,
       demultiplexer_1_out25, demultiplexer_1_out26, demultiplexer_1_out27, demultiplexer_1_out28,
       demultiplexer_1_out29, demultiplexer_1_out30, demultiplexer_1_out31;
  wire [31:0] undriven, undriven_2, undriven_3, undriven_4, undriven_5, undriven_6, undriven_7, undriven_8,
       undriven_9, undriven_10, undriven_11, undriven_12, undriven_13, undriven_14, undriven_15, undriven_16,
       undriven_17, undriven_18, undriven_19, undriven_20, undriven_21, undriven_22, undriven_23,
       undriven_24, undriven_25, undriven_26, undriven_27, undriven_28, undriven_29, undriven_30,
       undriven_31, undriven_32, undriven_33, undriven_34, undriven_35, undriven_36, undriven_37,
       undriven_38, undriven_39, undriven_40, undriven_41, undriven_42, undriven_43, undriven_44,
       undriven_45, undriven_46, undriven_47, undriven_48, undriven_49, undriven_50, undriven_51,
       undriven_52, undriven_53, undriven_54, undriven_55, undriven_56, undriven_57, undriven_58,
       undriven_59, undriven_60, undriven_61, undriven_62, undriven_63;

  Demultiplexer #(.select(5), .enable("false")) demultiplexer_1 (
    .out1(demultiplexer_1_out1), .out2(demultiplexer_1_out2), .out3(demultiplexer_1_out3),
    .out4(demultiplexer_1_out4), .out5(demultiplexer_1_out5), .out6(demultiplexer_1_out6),
    .out7(demultiplexer_1_out7), .out8(demultiplexer_1_out8), .out9(demultiplexer_1_out9),
    .out10(demultiplexer_1_out10), .out11(demultiplexer_1_out11), .out12(demultiplexer_1_out12),
    .out13(demultiplexer_1_out13), .out14(demultiplexer_1_out14), .out15(demultiplexer_1_out15),
    .out16(demultiplexer_1_out16), .out17(demultiplexer_1_out17), .out18(demultiplexer_1_out18),
    .out19(demultiplexer_1_out19), .out20(demultiplexer_1_out20), .out21(demultiplexer_1_out21),
    .out22(demultiplexer_1_out22), .out23(demultiplexer_1_out23), .out24(demultiplexer_1_out24),
    .out25(demultiplexer_1_out25), .out26(demultiplexer_1_out26), .out27(demultiplexer_1_out27),
    .out28(demultiplexer_1_out28), .out29(demultiplexer_1_out29), .out30(demultiplexer_1_out30),
    .out31(demultiplexer_1_out31), .in(WR), .sel(RegDEST));  // open: out0
  Reg0 reg0_1 (.dataIN(Data), .dataOUT(undriven), .S(undriven_32));
  Registrador registrador_1 (.WR(demultiplexer_1_out1), .dataIN(undriven), .dataOUT(undriven_2), .S(undriven_33));
  Registrador registrador_2 (.WR(demultiplexer_1_out2), .dataIN(undriven_2), .dataOUT(undriven_17), .S(undriven_34));
  Registrador registrador_3 (.WR(demultiplexer_1_out3), .dataIN(undriven_17), .dataOUT(undriven_18), .S(undriven_35));
  Registrador registrador_4 (.WR(demultiplexer_1_out4), .dataIN(undriven_18), .dataOUT(undriven_19), .S(undriven_52));
  Registrador registrador_5 (.WR(demultiplexer_1_out5), .dataIN(undriven_19), .dataOUT(undriven_3), .S(undriven_36));
  Registrador registrador_6 (.WR(demultiplexer_1_out6), .dataIN(undriven_3), .dataOUT(undriven_20), .S(undriven_37));
  Registrador registrador_7 (.WR(demultiplexer_1_out7), .dataIN(undriven_20), .dataOUT(undriven_21), .S(undriven_38));
  Registrador registrador_8 (.WR(demultiplexer_1_out8), .dataIN(undriven_21), .dataOUT(undriven_22), .S(undriven_53));
  Registrador registrador_9 (.WR(demultiplexer_1_out9), .dataIN(undriven_22), .dataOUT(undriven_4), .S(undriven_39));
  Registrador registrador_10 (.WR(demultiplexer_1_out10), .dataIN(undriven_4), .dataOUT(undriven_5), .S(undriven_54));
  Registrador registrador_11 (.WR(demultiplexer_1_out11), .dataIN(undriven_5), .dataOUT(undriven_23), .S(undriven_40));
  Registrador registrador_12 (.WR(demultiplexer_1_out12), .dataIN(undriven_23), .dataOUT(undriven_24), .S(undriven_55));
  Registrador registrador_13 (.WR(demultiplexer_1_out13), .dataIN(undriven_24), .dataOUT(undriven_6), .S(undriven_56));
  Registrador registrador_14 (.WR(demultiplexer_1_out14), .dataIN(undriven_6), .dataOUT(undriven_7), .S(undriven_57));
  Registrador registrador_15 (.WR(demultiplexer_1_out15), .dataIN(undriven_7), .dataOUT(undriven_25), .S(undriven_58));
  Registrador registrador_16 (.WR(demultiplexer_1_out16), .dataIN(undriven_25), .dataOUT(undriven_8), .S(undriven_41));
  Registrador registrador_17 (.WR(demultiplexer_1_out17), .dataIN(undriven_8), .dataOUT(undriven_9), .S(undriven_42));
  Registrador registrador_18 (.WR(demultiplexer_1_out18), .dataIN(undriven_9), .dataOUT(undriven_10), .S(undriven_43));
  Registrador registrador_19 (.WR(demultiplexer_1_out19), .dataIN(undriven_10), .dataOUT(undriven_26), .S(undriven_44));
  Registrador registrador_20 (.WR(demultiplexer_1_out20), .dataIN(undriven_26), .dataOUT(undriven_27), .S(undriven_45));
  Registrador registrador_21 (.WR(demultiplexer_1_out21), .dataIN(undriven_27), .dataOUT(undriven_11), .S(undriven_46));
  Registrador registrador_22 (.WR(demultiplexer_1_out22), .dataIN(undriven_11), .dataOUT(undriven_28), .S(undriven_59));
  Registrador registrador_23 (.WR(demultiplexer_1_out23), .dataIN(undriven_28), .dataOUT(undriven_29), .S(undriven_47));
  Registrador registrador_24 (.WR(demultiplexer_1_out24), .dataIN(undriven_29), .dataOUT(undriven_30), .S(undriven_60));
  Registrador registrador_25 (.WR(demultiplexer_1_out25), .dataIN(undriven_30), .dataOUT(undriven_12), .S(undriven_48));
  Registrador registrador_26 (.WR(demultiplexer_1_out26), .dataIN(undriven_12), .dataOUT(undriven_13), .S(undriven_61));
  Registrador registrador_27 (.WR(demultiplexer_1_out27), .dataIN(undriven_13), .dataOUT(undriven_14), .S(undriven_49));
  Registrador registrador_28 (.WR(demultiplexer_1_out28), .dataIN(undriven_14), .dataOUT(undriven_31), .S(undriven_62));
  Registrador registrador_29 (.WR(demultiplexer_1_out29), .dataIN(undriven_31), .dataOUT(undriven_15), .S(undriven_50));
  Registrador registrador_30 (.WR(demultiplexer_1_out30), .dataIN(undriven_15), .dataOUT(undriven_16), .S(undriven_63));
  Registrador registrador_31 (.WR(demultiplexer_1_out31), .dataIN(undriven_16), .S(undriven_51));  // open: dataOUT
  Multiplexer #(.select(5), .width(32), .enable("false")) multiplexer_1 (
    .in0(undriven_32), .in1(undriven_33), .in2(undriven_34), .in3(undriven_35), .in4(undriven_52),
    .in5(undriven_36), .in6(undriven_37), .in7(undriven_38), .in8(undriven_53), .in9(undriven_39),
    .in10(undriven_54), .in11(undriven_40), .in12(undriven_55), .in13(undriven_56), .in14(undriven_57),
    .in15(undriven_58), .in16(undriven_41), .in17(undriven_42), .in18(undriven_43), .in19(undriven_44),
    .in20(undriven_45), .in21(undriven_46), .in22(undriven_59), .in23(undriven_47), .in24(undriven_60),
    .in25(undriven_48), .in26(undriven_61), .in27(undriven_49), .in28(undriven_62), .in29(undriven_50),
    .in30(undriven_63), .in31(undriven_51), .out(RSout), .sel(RS));
  Multiplexer #(.select(5), .width(32), .enable("false")) multiplexer_2 (
    .in0(undriven_32), .in1(undriven_33), .in2(undriven_34), .in3(undriven_35), .in4(undriven_52),
    .in5(undriven_36), .in6(undriven_37), .in7(undriven_38), .in8(undriven_53), .in9(undriven_39),
    .in10(undriven_54), .in11(undriven_40), .in12(undriven_55), .in13(undriven_56), .in14(undriven_57),
    .in15(undriven_58), .in16(undriven_41), .in17(undriven_42), .in18(undriven_43), .in19(undriven_44),
    .in20(undriven_45), .in21(undriven_46), .in22(undriven_59), .in23(undriven_47), .in24(undriven_60),
    .in25(undriven_48), .in26(undriven_61), .in27(undriven_49), .in28(undriven_62), .in29(undriven_50),
    .in30(undriven_63), .in31(undriven_51), .out(RTout), .sel(RT));
endmodule

module Reg0 (
  input  [31:0] dataIN,
  input  [31:0] S,
  input  [31:0] dataOUT
);


  assign dataOUT = dataIN;
  // also tied to GND on the sheet: {S[0], S[1], S[2], S[3], S[4], S[5], S[6], S[7], S[8], S[9], S[10], S[11], S[12], S[13], S[14], S[15], S[16], S[17], S[18], S[19], S[20], S[21], S[22], S[23], S[24], S[25], S[26], S[27], S[28], S[29], S[30], S[31]}
endmodule

module main (
  input  [31:0] RS,
  input  [31:0] RT,
  input  [4:0] in_3,
  input  in_4,
  input  in_5,
  input  [11:0] DN,
  input  [4:0] Seletor_do_WR,
  input  [4:0] RS_2,
  input  [4:0] RT_2,
  output OVERFLOW,
  output ZERO
);

  wire [31:0] ula_1_s, undriven, undriven_2;

  _12bits_para_32_bits u_12bits_para_32_bits_1 (._12_BITS(DN), ._32_BITS(undriven_2));
  Banco_Registrador banco_registrador_1 (
    .Data(ula_1_s), .WR(in_4), .RegDEST(Seletor_do_WR), .RS(RS_2), .RT(RT_2), .RSout(RS), .RTout(undriven));
  Multiplexer #(.width(32), .enable("false")) multiplexer_1 (.in0(undriven), .in1(undriven_2), .out(RT), .sel(in_5));
  ULA ula_1 (.A(RS), .B(RT), .OVERFLOW(OVERFLOW), .SELETOR(in_3), .ZERO(ZERO), .S(ula_1_s));
endmodule

module _12bits_para_32_bits (
  input  [11:0] _12_BITS,
  input  [31:0] _32_BITS
);


  assign _32_BITS = {{21{_12_BITS[11]}}, _12_BITS[10:0]};
endmodule

module MicroPro (
  input  RESET,
  input  [31:0] \INSTRUÇÃO ,
  input  [31:0] RS,
  input  [31:0] RT,
  output OVERFLOW,
  output ZERO
);

  wire and_1_out, clock_1_out, d_ff_1_q, not_1_out, not_2_out;
  wire [7:0] pc_1_address;
  wire [31:0] ula_1_s, undriven, undriven_2;

  not not_1 (not_1_out, d_ff_1_q);
  Clock clock_1 (.out(clock_1_out));
  PC pc_1 (.ZERO(d_ff_1_q), .JUMP(\INSTRUÇÃO ), .RESET(RESET), .Address(pc_1_address));  // open: CLK
  D_Flip_Flop d_ff_1 (.clk(clock_1_out), .D(not_1_out), .Q(d_ff_1_q));  // open: Qn, preset, en, reset
  not not_2 (not_2_out, d_ff_1_q);
  _12bits_para_32_bits u_12bits_para_32_bits_1 (._12_BITS(\INSTRUÇÃO [11:0]), ._32_BITS(undriven_2));
  Banco_Registrador banco_registrador_1 (
    .Data(ula_1_s), .WR(not_2_out), .RegDEST(\INSTRUÇÃO [26:22]), .RS(\INSTRUÇÃO [21:17]),
    .RT(\INSTRUÇÃO [16:12]), .RSout(RS), .RTout(undriven));
  RAM #(.dataWidth(32)) ram_1 (.addr(pc_1_address), .data(\INSTRUÇÃO ));  // open: sel, clk, ld, clr
  and and_1 (and_1_out, ~\INSTRUÇÃO [27], ~\INSTRUÇÃO [28], \INSTRUÇÃO [29], \INSTRUÇÃO [30], ~\INSTRUÇÃO [31]);  // AND_Gate
  Multiplexer #(.width(32), .enable("false")) multiplexer_1 (
    .in0(undriven), .in1(undriven_2), .out(RT), .sel(and_1_out));
  ULA ula_1 (.A(RS), .B(RT), .OVERFLOW(OVERFLOW), .SELETOR(\INSTRUÇÃO [31:27]), .ZERO(ZERO), .S(ula_1_s));
endmodule

module PC (
  input  RESET,
  input  CLK,
  input  ZERO,
  input  [31:0] JUMP,
  output [7:0] Address
);

  wire and_1_out, and_2_out, and_3_out, and_4_out, and_5_out, or_1_out;
  wire [7:0] adder_1_out, multiplexer_1_out, multiplexer_2_out;

  and and_1 (and_1_out, ZERO, and_2_out);
  and and_2 (and_2_out, JUMP[0], ~JUMP[1], JUMP[2], JUMP[3], ~JUMP[4]);  // AND_Gate
  Multiplexer #(.width(8), .enable("false")) multiplexer_1 (
    .in0(8'h1), .in1(JUMP[31:24]), .out(multiplexer_1_out), .sel(or_1_out));
  or or_1 (or_1_out, and_1_out, and_3_out);
  and and_3 (and_3_out, ~ZERO, and_4_out);  // AND_Gate
  and and_4 (and_4_out, JUMP[0], ~JUMP[1], JUMP[2], JUMP[3], JUMP[4]);  // AND_Gate
  Register register_1 (.D(multiplexer_2_out), .Q(Address), .clk(CLK), .clr(RESET));  // open: en
  Adder adder_1 (.a(Address), .b(multiplexer_1_out), .out(adder_1_out), .cin(1'b0));  // open: cout
  Multiplexer #(.width(8), .enable("false")) multiplexer_2 (
    .in0(adder_1_out), .in1(JUMP[31:24]), .out(multiplexer_2_out), .sel(and_5_out));
  and and_5 (and_5_out, JUMP[0], ~JUMP[1], JUMP[2], ~JUMP[3], JUMP[4]);  // AND_Gate
endmodule
